# Fritzing sketch ldr-fog project (saved by Fritzing 0.9.4)

parts:
  Part1 = Arduino Nano (Rev3.0)
  R1 = Resistor [tolerance=±5% resistance=220 package=THT]
  R2 = Photocell (LDR) [package=THT]

nets:
  N1: Part1.GND, R2.pin_1
  N2: Part1.5V, R1.Pin_0
  N3: Part1.A0, R2.pin_0
